// Logisim project proj.circ as structural Verilog: 1 circuit, main circuit main
module main (
  input  bus_0
);

  wire cdm_16_1_p2, cdm_16_1_p4, cdm_16_1_p5, cdm_16_1_p6, cdm_16_1_p7, cdm_16_1_p8, cdm_16_1_p9,
       cdm_16_1_p10, clock_1_out;
  wire [15:0] cdm_16_1_p11, cdm_16_1_p12, multiplexer_1_out, rom_1_p4;

  // Probe on cdm_16_1_p2
  Clock clock_1 (.out(clock_1_out));
  // Probe on cdm_16_1_p5
  // Probe on cdm_16_1_p4
  // CdM_16 cdm_16_1: pin names not known; wires that end beside it: 1'b0, cdm_16_1_p2, clock_1_out, cdm_16_1_p4, cdm_16_1_p5, cdm_16_1_p6, cdm_16_1_p7, cdm_16_1_p8, cdm_16_1_p9, cdm_16_1_p10, cdm_16_1_p11, cdm_16_1_p12
  // Probe on cdm_16_1_p6
  // Probe on cdm_16_1_p7
  // Probe on cdm_16_1_p8
  // Probe on cdm_16_1_p11
  // Probe on cdm_16_1_p9
  // Probe on rom_1_p4
  // ROM rom_1: pin names not known; wires that end beside it: cdm_16_1_p11[7:0], 1'b1, 1'b1, rom_1_p4
  Multiplexer #(.width(16), .enable("false")) multiplexer_1 (
    .in0(16'h8a), .in1(16'h96), .out(multiplexer_1_out), .sel(bus_0));
  Multiplexer #(.width(16), .enable("false")) multiplexer_2 (
    .in0(rom_1_p4), .in1(multiplexer_1_out), .out(cdm_16_1_p12), .sel(cdm_16_1_p10));
  // Debugger debugger_1: pin names not known
endmodule
